# Fritzing sketch Diagrama Modulo SD (saved by Fritzing 0.9.3b)
breadboards: 1

parts:
  SD_card_module1 = SD Card Module
  Componente1 = Arduino Nano (Rev3.0)

nets:
  N1: SD_card_module1.+5, Componente1.5V
  N2: SD_card_module1.CS, Componente1.D10
  N3: SD_card_module1.MOSI, Componente1.D11/MOSI
  N4: SD_card_module1.SCK, Componente1.D13/SCK
  N5: SD_card_module1.MISO, Componente1.D12/MISO
  N6: SD_card_module1.GND#7, Componente1.GND

custom parts:
  SD Card Module: SD Card Module Slot Socket Reader For Arduino ARM MCU
